// Logisim project interrupt_detector.circ as structural Verilog: 1 circuit, main circuit interrupt_det
module interrupt_det (
  input  [7:0] in_1,
  input  rst,
  output out_3
);

  wire buffer_1_out, buffer_2_out, buffer_3_out, buffer_4_out, buffer_5_out, buffer_6_out, buffer_7_out,
       buffer_8_out, or_1_out, xor_1_out, xor_2_out, xor_3_out, xor_4_out, xor_5_out, xor_6_out, xor_7_out,
       xor_8_out;

  buf buffer_1 (buffer_1_out, in_1[0]);
  buf buffer_2 (buffer_2_out, in_1[1]);
  buf buffer_3 (buffer_3_out, in_1[2]);
  buf buffer_4 (buffer_4_out, in_1[3]);
  buf buffer_5 (buffer_5_out, in_1[4]);
  buf buffer_6 (buffer_6_out, in_1[5]);
  buf buffer_7 (buffer_7_out, in_1[6]);
  buf buffer_8 (buffer_8_out, in_1[7]);
  xor xor_1 (xor_1_out, in_1[0], buffer_1_out);
  xor xor_2 (xor_2_out, in_1[1], buffer_2_out);
  xor xor_3 (xor_3_out, in_1[2], buffer_3_out);
  xor xor_4 (xor_4_out, in_1[3], buffer_4_out);
  xor xor_5 (xor_5_out, in_1[4], buffer_5_out);
  xor xor_6 (xor_6_out, in_1[5], buffer_6_out);
  xor xor_7 (xor_7_out, in_1[6], buffer_7_out);
  xor xor_8 (xor_8_out, in_1[7], buffer_8_out);
  or or_1 (or_1_out, xor_1_out, xor_2_out, xor_3_out, xor_4_out, xor_5_out, xor_6_out, xor_7_out, xor_8_out);
  Register #(.width(1)) register_1 (.D(1'b1), .en(1'b1), .Q(out_3), .clk(or_1_out), .clr(rst));
endmodule
